// Logisim project 7SegmentDecoder.circ as structural Verilog: 2 circuits, main circuit SevenSegmentDecoder
module SevenSegmentDecoder (
  input  [3:0] IN_4_BIT,
  output A,
  output B,
  output C,
  output D,
  output E,
  output F,
  output G
);

  wire decoder_1_out0, decoder_1_out1, decoder_1_out2, decoder_1_out3, decoder_1_out4, decoder_1_out5,
       decoder_1_out6, decoder_1_out7, decoder_1_out9, decoder_1_out10, decoder_1_out11, decoder_1_out12,
       decoder_1_out13, decoder_1_out14, decoder_1_out15;

  Decoder #(.select(4)) decoder_1 (
    .out0(decoder_1_out0), .out1(decoder_1_out1), .out2(decoder_1_out2), .out3(decoder_1_out3),
    .out4(decoder_1_out4), .out5(decoder_1_out5), .out6(decoder_1_out6), .out7(decoder_1_out7),
    .out9(decoder_1_out9), .out10(decoder_1_out10), .out11(decoder_1_out11), .out12(decoder_1_out12),
    .out13(decoder_1_out13), .out14(decoder_1_out14), .out15(decoder_1_out15), .sel(IN_4_BIT));  // open: out8, en
  and and_1 (B, ~decoder_1_out1, ~decoder_1_out2, ~decoder_1_out3, ~decoder_1_out7, ~decoder_1_out13);  // AND_Gate
  and and_2 (A, ~decoder_1_out0, ~decoder_1_out1, ~decoder_1_out7, ~decoder_1_out12);  // AND_Gate
  and and_3 (C, ~decoder_1_out1, ~decoder_1_out4, ~decoder_1_out11, ~decoder_1_out13);  // AND_Gate
  and and_4 (D, ~decoder_1_out5, ~decoder_1_out6, ~decoder_1_out11, ~decoder_1_out12, ~decoder_1_out14, ~decoder_1_out15);  // AND_Gate
  and and_5 (E, ~decoder_1_out1, ~decoder_1_out3, ~decoder_1_out4, ~decoder_1_out5, ~decoder_1_out7, ~decoder_1_out9);  // AND_Gate
  and and_6 (F, ~decoder_1_out1, ~decoder_1_out4, ~decoder_1_out7, ~decoder_1_out9, ~decoder_1_out10, ~decoder_1_out15);  // AND_Gate
  and and_7 (G, ~decoder_1_out2, ~decoder_1_out12, ~decoder_1_out14, ~decoder_1_out15);  // AND_Gate
endmodule

module SevenSegmentToLCD (
  input  [3:0] in_1,
  output [6:0] out_2,
  output [6:0] out_3,
  output [6:0] out_4,
  output [6:0] out_5,
  output [6:0] out_6
);

  SevenSegmentDecoder sevensegmentdecoder_1 (
    .F(out_3[0]), .E(out_2[2]), .D(out_6[5]), .C(out_3[6]), .B(out_2[5]), .A(out_3[3]), .IN_4_BIT(in_1),
    .G(out_6[2]));

  assign {out_2[6], out_2[4:3], out_2[1:0]} = {1'b0, out_2[5], 1'b0, out_2[2], 1'b0};
  assign {out_3[5:4], out_3[2:1]} = 4'b0000;
  assign out_4 = {out_3[6], 2'b00, out_3[3], 2'b00, out_3[0]};
  assign out_5 = {out_3[6], 2'b00, out_3[3], 2'b00, out_3[0]};
  assign {out_6[6], out_6[4:3], out_6[1:0]} = {1'b0, out_6[5], 1'b0, out_6[2], 1'b0};
endmodule
