// Logisim project BinaryToDecimalConverter.circ as structural Verilog: 1 circuit, main circuit BinToDec8Bit
module BinToDec8Bit (
  input  [7:0] IN_8_BIT,
  output [3:0] HUNDREDS_DEC_4_BIT,
  output [3:0] TENS_DEC_4_BIT,
  output [3:0] ONES_DEC_4_BIT
);

  wire [7:0] divider_1_out;
  wire [7:4] divider_1_rem, divider_2_out, divider_2_rem;

  Divider divider_1 (
    .a(IN_8_BIT), .b(8'ha), .out(divider_1_out), .rem({divider_1_rem, ONES_DEC_4_BIT}));  // open: upper
  Divider divider_2 (
    .a(divider_1_out), .b(8'ha), .out({divider_2_out, HUNDREDS_DEC_4_BIT}),
    .rem({divider_2_rem, TENS_DEC_4_BIT}));  // open: upper
endmodule
