// Logisim project EdgeDetector.circ as structural Verilog: 4 circuits, main circuit Combined_Edge_Detector
module Combined_Edge_Detector (
  input  in_1,
  output out_2,
  output out_3
);

  wire not_1_out, not_2_out, not_3_out;

  not not_1 (not_1_out, in_1);
  and and_1 (out_2, in_1, not_2_out);
  not not_2 (not_2_out, in_1);
  and and_2 (out_3, not_1_out, not_3_out);
  not not_3 (not_3_out, not_1_out);
endmodule

module Rising_Edge_Detector (
  input  in_1,
  output out_2
);

  wire not_1_out;

  and and_1 (out_2, in_1, not_1_out);
  not not_1 (not_1_out, in_1);
endmodule

module Falling_Edge_Detector (
  input  in_1,
  output out_2
);

  wire not_1_out, not_2_out;

  not not_1 (not_1_out, in_1);
  and and_1 (out_2, not_1_out, not_2_out);
  not not_2 (not_2_out, not_1_out);
endmodule

module Bidirectional_Edge_Detector (
  input  in_1,
  output out_2
);

  wire and_1_out, and_2_out, not_1_out, not_2_out, not_3_out;

  not not_1 (not_1_out, in_1);
  and and_1 (and_1_out, in_1, not_2_out);
  not not_2 (not_2_out, in_1);
  and and_2 (and_2_out, not_1_out, not_3_out);
  not not_3 (not_3_out, not_1_out);
  or or_1 (out_2, and_1_out, and_2_out);
endmodule
